// Logisim project 1 circuit logism.circ as structural Verilog: 1 circuit, main circuit main
module main (
  input  i0,
  input  i1,
  output y
);

  wire g1_out, g2_out;

  or g1 (g1_out, i0, i1);
  nand g2 (g2_out, i0, i1);
  and and_1 (y, g1_out, g2_out);

  // Notes on the sheet:
  //   w1
  //   w2
endmodule
