// Logisim project 2 circut.circ as structural Verilog: 1 circuit, main circuit main
module main (
  input  i0,
  input  i1,
  output out_3
);

  wire G1_out, G2_out;

  and G1 (G1_out, i0, i1);
  or G2 (G2_out, i1, i0);
  nand G3 (out_3, G1_out, G2_out);

  // Notes on the sheet:
  //   w1
  //   w2
  //   Y
endmodule
