// Logisim project 3 circuit-logism.circ as structural Verilog: 1 circuit, main circuit main
module main (
  input  I0,
  input  I1,
  input  I2,
  output Y
);

  wire n7400_1_p3, n7400_1_p5;

  // _7400 7400_1: pin names not known; wires that end beside it: I0, I1, n7400_1_p3, n7400_1_p3, n7400_1_p5, Y
  // _7402 7402_1: pin names not known; wires that end beside it: n7400_1_p5, I2, I0
endmodule
