// Logisim project 4 circut.circ as structural Verilog: 1 circuit, main circuit main
module main (
  input  in_1,
  input  i1,
  output y
);

  wire G1_out, G2_out;

  or G1 (G1_out, in_1, i1);
  nand G2 (G2_out, in_1, G1_out);
  nor G3 (y, G2_out, i1);

  // Notes on the sheet:
  //   i0
  //   w1
  //   w2
endmodule
