// Logisim project 5 circut.circ as structural Verilog: 1 circuit, main circuit main
module main (
  input  i0,
  input  i1,
  output y
);

  wire G1_out;

  nor G1 (G1_out, i0, i1);
  nand G2 (y, G1_out, i1);

  // Notes on the sheet:
  //   w1
endmodule
